// Logisim project Kouachi.circ as structural Verilog: 1 circuit, main circuit Kouachi&hales_proc
module Kouachi_hales_proc (
  output [3:0] UAL_OUT
);

  wire clk, ri_1__11, ucc_1_out_4, ucc_1_out_5, ucc_1_out_6, ucc_1_out_7, ucc_1_out_8, ucc_1_out_9,
       ucc_1_out_10, ucc_1_out_11, ucc_1_out_12, ucc_1_out_13;
  wire [1:0] mux_2_1_2_bits_1_output, mux_2_1_2_bits_2_output, ri_1__1, ri_1__3, ri_1__4;
  wire [3:0] mux_2_1_4_bits_1_out_4, mux_2_1_4_bits_2_out_4, pc_counter_1_output, RA_output, ram_1_data,
       RD_output, rf_1_output_x, rf_1_output_y, ri_1__6, ual_1_equality;
  wire [11:0] rom_1_data;

  Clock clock_1 (.out(clk));
  PC__counter pc_counter_1 (.\output (pc_counter_1_output), .clk(clk), .enable(ucc_1_out_8));
  ROM #(.addrWidth(4), .dataWidth(12)) rom_1 (.addr(pc_counter_1_output), .data(rom_1_data));  // open: sel
  Mux_2_1__2_bits mux_2_1_2_bits_1 (
    .Input_0(ri_1__3), .Input_1(ri_1__4), .S(ucc_1_out_4), .Output(mux_2_1_2_bits_1_output));
  RF rf_1 (
    .Input(mux_2_1_4_bits_2_out_4), .Output_X(rf_1_output_x), .Output_Y(rf_1_output_y), .clk(clk),
    .Write(ucc_1_out_5), .Select(ri_1__4), .X(mux_2_1_2_bits_1_output), .Y(mux_2_1_2_bits_2_output));
  Mux_2_1__2_bits mux_2_1_2_bits_2 (
    .Input_0(ri_1__1), .Input_1(ri_1__3), .S(ucc_1_out_4), .Output(mux_2_1_2_bits_2_output));
  RI ri_1 (
    .\input (rom_1_data), .clk(clk), .Write(ucc_1_out_9), ._11(ri_1__11), ._9(ri_1__6[3]), ._8(ri_1__6[2]),
    ._7(ri_1__6[1]), ._6(ri_1__6[0]), ._5(ri_1__4[1]), ._4(ri_1__4[0]), ._3(ri_1__3[1]), ._2(ri_1__3[0]),
    ._1(ri_1__1[1]), ._0(ri_1__1[0]));  // open: _10
  UAL ual_1 (
    .Input_A(rf_1_output_x), .Input_B(rf_1_output_y), .Output(UAL_OUT), .Equality(ual_1_equality[0]),
    .Negative_Output(ual_1_equality[1]), .Overflow(ual_1_equality[2]), .ALU_OP__2_minus(ri_1__6[2]),
    .ALU_OP__1_minus(ri_1__6[1]), .ALU_OP__0_minus(ri_1__6[0]));
  Register__4_bits RE (.in_3(ual_1_equality), .Write(ucc_1_out_12), .clk(clk));  // open: Output
  UCC ucc_1 (
    .Input(ri_1__11), .OPcode(ri_1__6), .clk(clk), .out_4(ucc_1_out_4), .out_5(ucc_1_out_5),
    .out_6(ucc_1_out_6), .out_7(ucc_1_out_7), .out_8(ucc_1_out_8), .out_9(ucc_1_out_9),
    .out_10(ucc_1_out_10), .out_11(ucc_1_out_11), .out_12(ucc_1_out_12), .out_13(ucc_1_out_13));
  Mux_2_1__4_bits mux_2_1_4_bits_1 (
    .in_2(rf_1_output_x), .in_3(ram_1_data), .out_4(mux_2_1_4_bits_1_out_4), .in_1(ucc_1_out_7));
  Mux_2_1__4_bits mux_2_1_4_bits_2 (
    .in_2(RD_output), .in_3(UAL_OUT), .out_4(mux_2_1_4_bits_2_out_4), .in_1(ucc_1_out_6));
  Register__4_bits RA (
    .in_3({ri_1__1[0], ri_1__1[1], ri_1__3[0], ri_1__3[1]}), .Output(RA_output), .Write(ucc_1_out_11),
    .clk(clk));
  Register__4_bits RD (.in_3(mux_2_1_4_bits_1_out_4), .Output(RD_output), .Write(ucc_1_out_10), .clk(clk));
  RAM #(.addrWidth(4), .dataWidth(4), .bus("separate")) ram_1 (
    .addr(RA_output), .din(RD_output), .data(ram_1_data), .str(ucc_1_out_13), .clk(clk), .ld(1'b1));  // open: sel, clr

  // Notes on the sheet:
  //   Kouachi Ilyes & Hales Salim G:03
  //   contents of rom_1 (hex, n*v repeats v):
  //   a04 a12 78 a74
endmodule
