// Logisim project Ilyes_Kouachi_cpu.circ as structural Verilog: 5 circuits, main circuit Kouachi_proc
module Kouachi_proc (
  input  RESET
);

  wire clk, PC_plus_plus, undriven;
  wire [2:0] counter_1_q;
  wire [3:0] ir_1_opcode;
  wire [11:0] rom_1_data;

  Clock clock_1 (.out(clk));
  Counter #(.width(3), .max('h7)) counter_1 (
    .count(PC_plus_plus), .Q(counter_1_q), .clk(undriven), .clr(RESET));  // open: load, D, carry
  ROM #(.addrWidth(3), .dataWidth(12)) rom_1 (.addr(counter_1_q), .data(rom_1_data));  // open: sel
  IR ir_1 (.Input(rom_1_data), .OPCODE(ir_1_opcode));  // open: M_U, R1, R2, R3, Imm
  // PCU pcu_1: pin names not known; wires that end beside it: ir_1_opcode
endmodule

module IR (
  input  [11:0] Input,
  output [1:0] M_U,
  output [3:0] OPCODE,
  output [1:0] R1,
  output [1:0] R2,
  output [1:0] R3,
  output [3:0] Imm
);


  assign Imm = Input[3:0];
  assign M_U = Input[11:10];
  assign OPCODE = Input[9:6];
  assign R1 = Input[5:4];
  assign R2 = Input[3:2];
  assign R3 = Input[1:0];
endmodule

module PCU (
  input  M,
  input  [3:0] inOPCODE
);

  wire clk, or_1_out;
  wire [4:0] car_1_output, mapper_1_control_address, multiplexer_1_out, rom_1_data;
  wire [15:5] rom_1_data_2;

  Mapper mapper_1 (.control_address(mapper_1_control_address), .opcode(inOPCODE));
  Multiplexer #(.width(5), .enable("false")) multiplexer_1 (
    .in0(mapper_1_control_address), .in1(rom_1_data), .out(multiplexer_1_out), .sel(rom_1_data_2[5]));
  or or_1 (or_1_out, M, ~rom_1_data_2[6]);  // OR_Gate
  CAR car_1 (.\input (multiplexer_1_out), .\output (car_1_output), .clk(clk), .Write(or_1_out));
  ROM #(.addrWidth(5), .dataWidth(16)) rom_1 (.addr(car_1_output), .data({rom_1_data_2, rom_1_data}));  // open: sel

  // Notes on the sheet:
  //   contents of rom_1 (hex, n*v repeats v):
  //   2001 5802 8003 c018 2005 1806 8007 18 2009 780a a00b 18 211 a012 18 0 415 1016 18 0 a019 612 193 0
  //   813
endmodule

module Mapper (
  input  [3:0] opcode,
  output [4:0] control_address
);

  wire or_1_out, or_2_out;

  or or_1 (or_1_out, opcode[3], opcode[2]);
  and and_1 (control_address[3], opcode[2], ~opcode[1], ~opcode[0]);  // AND_Gate
  and and_2 (control_address[2], or_1_out, or_2_out);
  or or_2 (or_2_out, opcode[1], opcode[0]);

  assign {control_address[4], control_address[1:0]} = {opcode[3], 2'b00};
endmodule

module CAR (
  input  clk,
  input  Write,
  input  [4:0] \input ,
  output [4:0] \output 
);

  wire not_1_out;

  Counter #(.width(5), .max('h1f)) counter_1 (
    .load(Write), .D(\input ), .count(not_1_out), .Q(\output ), .clk(clk));  // open: carry, clr
  not not_1 (not_1_out, Write);
endmodule
