// Logisim project Processeur.circ as structural Verilog: 24 circuits, main circuit CPU
module CPU (
  input  in_1
);

  wire ARw, clk, instruction_register_1__10, instruction_register_1__11, IRw, PC_plus_plus, RDsrc, RDw,
       RFsrc, RFw, RFxy, SRW, Store;
  wire [1:0] instruction_register_1__0, instruction_register_1__2, instruction_register_1__4,
       multiplexer_1_out, multiplexer_2_out;
  wire [3:0] alu_1_output, alu_1_status_register, ar_address_register_1_output, dr_data_register_1_output,
       instruction_register_1__9, multiplexer_3_out, multiplexer_4_out,
       pc_programe_counter_register_1_output, ram_1_data, rf_rgister_file_4x4_bits_1_x_output,
       rf_rgister_file_4x4_bits_1_y_output;
  wire [11:0] rom_1_data;

  Clock clock_1 (.out(clk));
  PC_Programe_Counter_Register pc_programe_counter_register_1 (
    .\output (pc_programe_counter_register_1_output), .clk(clk), .count_enable(PC_plus_plus), .in_3(in_1));
  RF_Rgister_File__4x4_bits rf_rgister_file_4x4_bits_1 (
    .Input(multiplexer_4_out), .X_output(rf_rgister_file_4x4_bits_1_x_output), .clk(clk),
    .dst(instruction_register_1__4), .X(multiplexer_1_out), .Y(multiplexer_2_out), .write(RFw),
    .Y_output(rf_rgister_file_4x4_bits_1_y_output));
  ROM #(.addrWidth(4), .dataWidth(12)) rom_1 (
    .addr(pc_programe_counter_register_1_output), .data(rom_1_data));  // open: sel
  Multiplexer #(.width(2), .enable("false")) multiplexer_1 (
    .in0(instruction_register_1__4), .in1(instruction_register_1__2), .out(multiplexer_1_out), .sel(RFxy));
  Hex_Digit_Display hex_digit_display_1 (.value(pc_programe_counter_register_1_output));  // open: dp
  Multiplexer #(.width(2), .enable("false")) multiplexer_2 (
    .in0(instruction_register_1__2), .in1(instruction_register_1__0), .out(multiplexer_2_out), .sel(RFxy));
  Hex_Digit_Display hex_digit_display_2 (.value(rf_rgister_file_4x4_bits_1_x_output));  // open: dp
  Hex_Digit_Display hex_digit_display_3 (.value(rf_rgister_file_4x4_bits_1_y_output));  // open: dp
  ALU alu_1 (
    .Input_A(rf_rgister_file_4x4_bits_1_x_output), .Input_B(rf_rgister_file_4x4_bits_1_y_output),
    .Output(alu_1_output), .ALU_OP(instruction_register_1__9[2:0]), .Status_register(alu_1_status_register));
  UCC ucc_1 (
    .clk(clk), .CodeOp(instruction_register_1__9), .M(instruction_register_1__11), .MEMw(Store), .DRW(RDw),
    .IRW(IRw), .DRsrc(RDsrc), .xySrc(RFxy), .FRsrc(RFsrc), .PC_plus_plus(PC_plus_plus), .ARW(ARw), .SRW(SRW));
  Instruction_Register instruction_register_1 (
    .\input (rom_1_data), ._0(instruction_register_1__0[0]), ._1(instruction_register_1__0[1]),
    ._3(instruction_register_1__2[1]), ._2(instruction_register_1__2[0]), ._7(instruction_register_1__9[1]),
    ._6(instruction_register_1__9[0]), ._5(instruction_register_1__4[1]), ._4(instruction_register_1__4[0]),
    ._11(instruction_register_1__11), ._10(instruction_register_1__10), ._9(instruction_register_1__9[3]),
    ._8(instruction_register_1__9[2]));
  Hex_Digit_Display hex_digit_display_4 (.value(alu_1_output));  // open: dp
  Hex_Digit_Display hex_digit_display_5 (.value({instruction_register_1__2, instruction_register_1__0}));  // open: dp
  Hex_Digit_Display hex_digit_display_6 (.value(multiplexer_3_out));  // open: dp
  Multiplexer #(.width(4), .enable("false")) multiplexer_3 (
    .in0(rf_rgister_file_4x4_bits_1_x_output), .in1(ram_1_data), .out(multiplexer_3_out), .sel(RDsrc));
  SR_Status_Register sr_status_register_1 (.\input (alu_1_status_register), .clk(clk), .Write(SRW));  // open: output
  AR_Address_Register ar_address_register_1 (
    .\input ({instruction_register_1__2, instruction_register_1__0}),
    .\output (ar_address_register_1_output), .clk(clk), .Write(ARw));
  DR_Data_Register dr_data_register_1 (
    .\input (multiplexer_3_out), .\output (dr_data_register_1_output), .clk(clk), .Write(RDw));
  Hex_Digit_Display hex_digit_display_7 (.value(ar_address_register_1_output));  // open: dp
  Multiplexer #(.width(4), .enable("false")) multiplexer_4 (
    .in0(alu_1_output), .in1(dr_data_register_1_output), .out(multiplexer_4_out), .sel(RFsrc));
  RAM #(.addrWidth(4), .dataWidth(4), .bus("separate")) ram_1 (
    .addr(ar_address_register_1_output), .din(dr_data_register_1_output), .data(ram_1_data), .str(Store),
    .clk(clk), .ld(1'b1));  // open: sel, clr

  // Other names for the same wires on the sheet: A = in_1

  // Notes on the sheet:
  //   PGM ROM
  //   contents of rom_1 (hex, n*v repeats v):
  //   a13 a23 56 a50
  //   DATA RAM
endmodule

module UCC (
  input  clk,
  input  M,
  input  [3:0] CodeOp,
  output xySrc,
  output FRsrc,
  output DRsrc,
  output PC_plus_plus,
  output IRW,
  output ARW,
  output DRW,
  output SRW,
  output MEMw
);

  wire or_1_out;
  wire [4:0] car_control_address_register_1_output, mapper_1_control_address, multiplexer_1_out, rom_1_data;
  wire [6:5] rom_1_data_2;

  Multiplexer #(.width(5), .enable("false")) multiplexer_1 (
    .in0(mapper_1_control_address), .in1(rom_1_data), .out(multiplexer_1_out), .sel(rom_1_data_2[5]));
  Mapper mapper_1 (.control_address(mapper_1_control_address), .opcode(CodeOp));
  CAR_Control_Address_Register car_control_address_register_1 (
    .clk(clk), .Write(or_1_out), .\output (car_control_address_register_1_output), .\input (multiplexer_1_out));
  or or_1 (or_1_out, M, ~rom_1_data_2[6]);  // OR_Gate
  ROM #(.addrWidth(5), .dataWidth(16)) rom_1 (
    .addr(car_control_address_register_1_output),
    .data({xySrc, FRsrc, DRsrc, PC_plus_plus, IRW, ARW, DRW, SRW, MEMw, rom_1_data_2, rom_1_data}));  // open: sel

  // Notes on the sheet:
  //   Micro-code ROM
  //   contents of rom_1 (hex, n*v repeats v):
  //   2001 5802 8003 c018 2005 1806 8007 18 2009 780a a00b 18 211 a012 18 0 415 1016 18 0 a019 612 193 0
  //   813
endmodule

// RF
module RF_Rgister_File__4x4_bits (
  input  clk,
  input  write,
  input  [1:0] dst,
  input  [1:0] X,
  input  [1:0] Y,
  input  [3:0] Input,
  output [3:0] X_output,
  output [3:0] Y_output
);

  wire and_1_out, and_2_out, and_3_out, and_4_out, decoder_1_out0, decoder_1_out1, decoder_1_out2,
       decoder_1_out3;
  wire [3:0] registre_4_bits_1_output, registre_4_bits_2_output, registre_4_bits_3_output,
       registre_4_bits_4_output;

  Decoder #(.select(2), .enable("false")) decoder_1 (
    .out0(decoder_1_out0), .out1(decoder_1_out1), .out2(decoder_1_out2), .out3(decoder_1_out3), .sel(dst));
  and and_1 (and_1_out, write, decoder_1_out0);
  Registre_4_bits registre_4_bits_1 (
    .\input (Input), .\output (registre_4_bits_1_output), .clk(clk), .Write(and_1_out));
  and and_2 (and_2_out, write, decoder_1_out1);
  Registre_4_bits registre_4_bits_2 (
    .\input (Input), .\output (registre_4_bits_2_output), .clk(clk), .Write(and_2_out));
  and and_3 (and_3_out, write, decoder_1_out2);
  Registre_4_bits registre_4_bits_3 (
    .\input (Input), .\output (registre_4_bits_3_output), .clk(clk), .Write(and_3_out));
  and and_4 (and_4_out, write, decoder_1_out3);
  Registre_4_bits registre_4_bits_4 (
    .\input (Input), .\output (registre_4_bits_4_output), .clk(clk), .Write(and_4_out));
  Multiplexer #(.select(2), .width(4), .enable("false")) multiplexer_1 (
    .in0(registre_4_bits_1_output), .in1(registre_4_bits_2_output), .in2(registre_4_bits_3_output),
    .in3(registre_4_bits_4_output), .out(X_output), .sel(X));
  Multiplexer #(.select(2), .width(4), .enable("false")) multiplexer_2 (
    .in0(registre_4_bits_1_output), .in1(registre_4_bits_2_output), .in2(registre_4_bits_3_output),
    .in3(registre_4_bits_4_output), .out(Y_output), .sel(Y));
endmodule

// PC
module PC_Programe_Counter_Register (
  input  clk,
  input  count_enable,
  input  in_3,
  output [3:0] \output 
);

  Counter #(.width(4), .max('hf)) counter_1 (
    .count(count_enable), .Q(\output ), .clk(clk), .clr(in_3));  // open: load, D, carry
endmodule

// IR
module Instruction_Register (
  input  [11:0] \input ,
  output _11,
  output _10,
  output _9,
  output _8,
  output _7,
  output _6,
  output _5,
  output _4,
  output _3,
  output _2,
  output _1,
  output _0
);


  assign _0 = \input [0];
  assign _1 = \input [1];
  assign _2 = \input [2];
  assign _3 = \input [3];
  assign _4 = \input [4];
  assign _5 = \input [5];
  assign _6 = \input [6];
  assign _7 = \input [7];
  assign _8 = \input [8];
  assign _9 = \input [9];
  assign _10 = \input [10];
  assign _11 = \input [11];
endmodule

// DR
module DR_Data_Register (
  input  clk,
  input  Write,
  input  [3:0] \input ,
  output [3:0] \output 
);

  D_Flip_Flop d_ff_1 (.clk(clk), .D(\input [0]), .Q(\output [0]), .en(Write));  // open: Qn, preset, reset
  D_Flip_Flop d_ff_2 (.clk(clk), .D(\input [1]), .Q(\output [1]), .en(Write));  // open: Qn, preset, reset
  D_Flip_Flop d_ff_3 (.clk(clk), .D(\input [2]), .Q(\output [2]), .en(Write));  // open: Qn, preset, reset
  D_Flip_Flop d_ff_4 (.clk(clk), .D(\input [3]), .Q(\output [3]), .en(Write));  // open: Qn, preset, reset
endmodule

// AR
module AR_Address_Register (
  input  clk,
  input  Write,
  input  [3:0] \input ,
  output [3:0] \output 
);

  D_Flip_Flop d_ff_1 (.clk(clk), .D(\input [0]), .Q(\output [0]), .en(Write));  // open: Qn, preset, reset
  D_Flip_Flop d_ff_2 (.clk(clk), .D(\input [1]), .Q(\output [1]), .en(Write));  // open: Qn, preset, reset
  D_Flip_Flop d_ff_3 (.clk(clk), .D(\input [2]), .Q(\output [2]), .en(Write));  // open: Qn, preset, reset
  D_Flip_Flop d_ff_4 (.clk(clk), .D(\input [3]), .Q(\output [3]), .en(Write));  // open: Qn, preset, reset
endmodule

// SR
module SR_Status_Register (
  input  clk,
  input  Write,
  input  [3:0] \input ,
  output [3:0] \output 
);

  D_Flip_Flop d_ff_1 (.clk(clk), .D(\input [0]), .Q(\output [0]), .en(Write));  // open: Qn, preset, reset
  D_Flip_Flop d_ff_2 (.clk(clk), .D(\input [1]), .Q(\output [1]), .en(Write));  // open: Qn, preset, reset
  D_Flip_Flop d_ff_3 (.clk(clk), .D(\input [2]), .Q(\output [2]), .en(Write));  // open: Qn, preset, reset
  D_Flip_Flop d_ff_4 (.clk(clk), .D(\input [3]), .Q(\output [3]), .en(Write));  // open: Qn, preset, reset
endmodule

// CAR
module CAR_Control_Address_Register (
  input  clk,
  input  Write,
  input  [4:0] \input ,
  output [4:0] \output 
);

  Counter #(.width(5), .max('h1f)) counter_1 (
    .D(\input ), .count(Write), .Q(\output ), .clk(clk));  // open: load, carry, clr
endmodule

// CSR
module CSR_Control_Signals_Register (
  input  clk,
  input  Write,
  input  [16:0] \input ,
  output RFxy,
  output RFsrc,
  output PC_plus_plus,
  output ARw,
  output SRw,
  output CD,
  output BR,
  output AD4,
  output AD3,
  output AD2,
  output AD1,
  output AD0,
  output RFw,
  output DRsrc,
  output IRw,
  output DRw,
  output MEMw
);

  D_Flip_Flop d_ff_1 (.clk(clk), .D(\input [0]), .Q(AD0), .en(Write));  // open: Qn, preset, reset
  D_Flip_Flop d_ff_2 (.clk(clk), .D(\input [1]), .Q(AD1), .en(Write));  // open: Qn, preset, reset
  D_Flip_Flop d_ff_3 (.clk(clk), .D(\input [2]), .Q(AD2), .en(Write));  // open: Qn, preset, reset
  D_Flip_Flop d_ff_4 (.clk(clk), .D(\input [3]), .Q(AD3), .en(Write));  // open: Qn, preset, reset
  D_Flip_Flop d_ff_5 (.clk(clk), .D(\input [4]), .Q(AD4), .en(Write));  // open: Qn, preset, reset
  D_Flip_Flop d_ff_6 (.clk(clk), .D(\input [5]), .Q(BR), .en(Write));  // open: Qn, preset, reset
  D_Flip_Flop d_ff_7 (.clk(clk), .D(\input [6]), .Q(CD), .en(Write));  // open: Qn, preset, reset
  D_Flip_Flop d_ff_8 (.clk(clk), .D(\input [7]), .Q(MEMw), .en(Write));  // open: Qn, preset, reset
  D_Flip_Flop d_ff_9 (.clk(clk), .D(\input [8]), .Q(SRw), .en(Write));  // open: Qn, preset, reset
  D_Flip_Flop d_ff_10 (.clk(clk), .D(\input [9]), .Q(DRw), .en(Write));  // open: Qn, preset, reset
  D_Flip_Flop d_ff_11 (.clk(clk), .D(\input [10]), .Q(ARw), .en(Write));  // open: Qn, preset, reset
  D_Flip_Flop d_ff_12 (.clk(clk), .D(\input [11]), .Q(IRw), .en(Write));  // open: Qn, preset, reset
  D_Flip_Flop d_ff_13 (.clk(clk), .D(\input [12]), .Q(PC_plus_plus), .en(Write));  // open: Qn, preset, reset
  D_Flip_Flop d_ff_14 (.clk(clk), .D(\input [13]), .Q(DRsrc), .en(Write));  // open: Qn, preset, reset
  D_Flip_Flop d_ff_15 (.clk(clk), .D(\input [14]), .Q(RFsrc), .en(Write));  // open: Qn, preset, reset
  D_Flip_Flop d_ff_16 (.clk(clk), .D(\input [15]), .Q(RFw), .en(Write));  // open: Qn, preset, reset
  D_Flip_Flop d_ff_17 (.clk(clk), .D(\input [16]), .Q(RFxy), .en(Write));  // open: Qn, preset, reset
endmodule

// <<
module Shifter_Left (
  input  C1,
  input  C0,
  input  [3:0] Input,
  output [3:0] Output
);

  Mux_4_1 mux_4_1_1 (
    .Input_0(Input[0]), .Input_1(1'b0), .Input_2(1'b0), .Input_3(1'b0), .Output(Output[0]), .Select_0(C0),
    .Select_1(C1));
  Mux_4_1 mux_4_1_2 (
    .Input_0(Input[1]), .Input_1(Input[0]), .Input_2(1'b0), .Input_3(1'b0), .Output(Output[1]),
    .Select_0(C0), .Select_1(C1));
  Mux_4_1 mux_4_1_3 (
    .Input_0(Input[2]), .Input_1(Input[1]), .Input_2(Input[0]), .Input_3(1'b0), .Output(Output[2]),
    .Select_0(C0), .Select_1(C1));
  Mux_4_1 mux_4_1_4 (
    .Input_0(Input[3]), .Input_1(Input[2]), .Input_2(Input[1]), .Input_3(Input[0]), .Output(Output[3]),
    .Select_0(C0), .Select_1(C1));
endmodule

// >>
module Shifter_Right (
  input  C1,
  input  C0,
  input  [3:0] Input,
  output [3:0] Output
);

  Mux_4_1 mux_4_1_1 (
    .Input_0(Input[0]), .Input_1(Input[1]), .Input_2(Input[2]), .Input_3(Input[3]), .Output(Output[0]),
    .Select_0(C0), .Select_1(C1));
  Mux_4_1 mux_4_1_2 (
    .Input_0(Input[1]), .Input_1(Input[2]), .Input_2(Input[3]), .Input_3(1'b0), .Output(Output[1]),
    .Select_0(C0), .Select_1(C1));
  Mux_4_1 mux_4_1_3 (
    .Input_0(Input[2]), .Input_1(Input[3]), .Input_2(1'b0), .Input_3(1'b0), .Output(Output[2]),
    .Select_0(C0), .Select_1(C1));
  Mux_4_1 mux_4_1_4 (
    .Input_0(Input[3]), .Input_1(1'b0), .Input_2(1'b0), .Input_3(1'b0), .Output(Output[3]), .Select_0(C0),
    .Select_1(C1));
endmodule

module Mapper (
  input  [3:0] opcode,
  output [4:0] control_address
);

  wire or_1_out, or_2_out;

  or or_1 (or_1_out, opcode[3], opcode[2]);
  and and_1 (control_address[3], opcode[2], ~opcode[1], ~opcode[0]);  // AND_Gate
  and and_2 (control_address[2], or_1_out, or_2_out);
  or or_2 (or_2_out, opcode[1], opcode[0]);

  assign {control_address[4], control_address[1:0]} = {opcode[3], 2'b00};
endmodule

module Registre_4_bits (
  input  clk,
  input  Write,
  input  [3:0] \input ,
  output [3:0] \output 
);

  D_Flip_Flop d_ff_1 (.clk(clk), .D(\input [0]), .Q(\output [0]), .en(Write));  // open: Qn, preset, reset
  D_Flip_Flop d_ff_2 (.clk(clk), .D(\input [1]), .Q(\output [1]), .en(Write));  // open: Qn, preset, reset
  D_Flip_Flop d_ff_3 (.clk(clk), .D(\input [2]), .Q(\output [2]), .en(Write));  // open: Qn, preset, reset
  D_Flip_Flop d_ff_4 (.clk(clk), .D(\input [3]), .Q(\output [3]), .en(Write));  // open: Qn, preset, reset
endmodule

module Adder_4_bits (
  input  Cin,
  input  [3:0] A,
  input  [3:0] B,
  output [3:0] Sum,
  output overflow,
  output Cout
);

  wire full_adder_1_cout, full_adder_2_cout, full_adder_3_cout;

  Full_Adder full_adder_1 (.A(A[0]), .B(B[0]), .S(Sum[0]), .Cin(Cin), .Cout(full_adder_1_cout));
  Full_Adder full_adder_2 (.A(A[1]), .B(B[1]), .S(Sum[1]), .Cin(full_adder_1_cout), .Cout(full_adder_2_cout));
  Full_Adder full_adder_3 (.A(A[2]), .B(B[2]), .S(Sum[2]), .Cin(full_adder_2_cout), .Cout(full_adder_3_cout));
  Full_Adder full_adder_4 (.A(A[3]), .B(B[3]), .S(Sum[3]), .Cin(full_adder_3_cout), .Cout(Cout));
  xor xor_1 (overflow, full_adder_3_cout, Cout);
endmodule

module Full_Adder (
  input  Cin,
  input  A,
  input  B,
  output S,
  output Cout
);

  wire and_1_out, and_2_out, and_3_out;

  xor xor_1 (S, A, B, Cin);
  and and_1 (and_1_out, A, B);
  and and_2 (and_2_out, A, Cin);
  and and_3 (and_3_out, B, Cin);
  or or_1 (Cout, and_1_out, and_2_out, and_3_out);
endmodule

module Mux_2_1 (
  input  Select,
  input  Input_0,
  input  Input_1,
  output Output
);

  wire and_1_out, and_2_out, not_1_out;

  not not_1 (not_1_out, Select);
  and and_1 (and_1_out, not_1_out, Input_0);
  and and_2 (and_2_out, Select, Input_1);
  or or_1 (Output, and_1_out, and_2_out);
endmodule

// Mux 2-1
module Mux_2_1__2_bits (
  input  Select,
  input  [1:0] Input_0,
  input  [1:0] Input_1,
  output [1:0] Output
);

  Mux_2_1 mux_2_1_1 (.Input_0(Input_0[0]), .Input_1(Input_1[0]), .Output(Output[0]), .Select(Select));
  Mux_2_1 mux_2_1_2 (.Input_0(Input_0[1]), .Input_1(Input_1[1]), .Output(Output[1]), .Select(Select));
endmodule

// Mux 2-1
module Mux_2_1__4_bits (
  input  Select,
  input  [3:0] Input_0,
  input  [3:0] Input_1,
  output [3:0] Output
);

  Mux_2_1 mux_2_1_1 (.Input_0(Input_0[0]), .Input_1(Input_1[0]), .Output(Output[0]), .Select(Select));
  Mux_2_1 mux_2_1_2 (.Input_0(Input_0[1]), .Input_1(Input_1[1]), .Output(Output[1]), .Select(Select));
  Mux_2_1 mux_2_1_3 (.Input_0(Input_0[2]), .Input_1(Input_1[2]), .Output(Output[2]), .Select(Select));
  Mux_2_1 mux_2_1_4 (.Input_0(Input_0[3]), .Input_1(Input_1[3]), .Output(Output[3]), .Select(Select));
endmodule

// Mux 2-1
module Mux_2_1__5_bits (
  input  Select,
  input  [4:0] Input_0,
  input  [4:0] Input_1,
  output [4:0] Output
);

  Mux_2_1 mux_2_1_1 (.Input_0(Input_0[0]), .Input_1(Input_1[0]), .Output(Output[0]), .Select(Select));
  Mux_2_1 mux_2_1_2 (.Input_0(Input_0[1]), .Input_1(Input_1[1]), .Output(Output[1]), .Select(Select));
  Mux_2_1 mux_2_1_3 (.Input_0(Input_0[2]), .Input_1(Input_1[2]), .Output(Output[2]), .Select(Select));
  Mux_2_1 mux_2_1_4 (.Input_0(Input_0[3]), .Input_1(Input_1[3]), .Output(Output[3]), .Select(Select));
  Mux_2_1 mux_2_1_5 (.Input_0(Input_0[4]), .Input_1(Input_1[4]), .Output(Output[4]), .Select(Select));
endmodule

module Mux_4_1 (
  input  Select_0,
  input  Select_1,
  input  Input_0,
  input  Input_1,
  input  Input_2,
  input  Input_3,
  output Output
);

  wire mux_2_1_1_output, mux_2_1_2_output;

  Mux_2_1 mux_2_1_1 (.Input_0(Input_0), .Input_1(Input_1), .Output(mux_2_1_1_output), .Select(Select_0));
  Mux_2_1 mux_2_1_2 (.Input_0(Input_2), .Input_1(Input_3), .Output(mux_2_1_2_output), .Select(Select_0));
  Mux_2_1 mux_2_1_3 (.Input_0(mux_2_1_1_output), .Input_1(mux_2_1_2_output), .Output(Output), .Select(Select_1));
endmodule

// Mux 4-1
module Mux_4_1__4_bits (
  input  Select_0,
  input  Select_1,
  input  [3:0] Input_0,
  input  [3:0] Input_1,
  input  [3:0] Input_2,
  input  [3:0] Input_3,
  output [3:0] Output
);

  wire [3:0] mux_2_1_4_bits_1_output, mux_2_1_4_bits_2_output;

  Mux_2_1__4_bits mux_2_1_4_bits_1 (
    .Input_0(Input_0), .Input_1(Input_1), .Output(mux_2_1_4_bits_1_output), .Select(Select_0));
  Mux_2_1__4_bits mux_2_1_4_bits_2 (
    .Input_0(Input_2), .Input_1(Input_3), .Output(mux_2_1_4_bits_2_output), .Select(Select_0));
  Mux_2_1__4_bits mux_2_1_4_bits_3 (
    .Input_0(mux_2_1_4_bits_1_output), .Input_1(mux_2_1_4_bits_2_output), .Output(Output), .Select(Select_1));
endmodule

// Mux 8-1
module Mux_8_1__4_bits (
  input  Select_1,
  input  Select_0,
  input  Select_2,
  input  [3:0] Input_0,
  input  [3:0] Input_1,
  input  [3:0] Input_2,
  input  [3:0] Input_3,
  input  [3:0] Input_4,
  input  [3:0] Input_5,
  input  [3:0] Input_6,
  input  [3:0] Input_7,
  output [3:0] Output
);

  wire [3:0] mux_4_1_4_bits_1_output, mux_4_1_4_bits_2_output;

  Mux_4_1__4_bits mux_4_1_4_bits_1 (
    .Input_0(Input_0), .Input_1(Input_1), .Input_2(Input_2), .Input_3(Input_3),
    .Output(mux_4_1_4_bits_1_output), .Select_0(Select_0), .Select_1(Select_1));
  Mux_4_1__4_bits mux_4_1_4_bits_2 (
    .Input_0(Input_4), .Input_1(Input_5), .Input_2(Input_6), .Input_3(Input_7),
    .Output(mux_4_1_4_bits_2_output), .Select_0(Select_0), .Select_1(Select_1));
  Mux_2_1__4_bits mux_2_1_4_bits_1 (
    .Input_0(mux_4_1_4_bits_1_output), .Input_1(mux_4_1_4_bits_2_output), .Output(Output), .Select(Select_2));
endmodule

module Decoder_2_4 (
  input  Input_1,
  input  Input_0,
  output out_3,
  output out_4,
  output out_5,
  output out_6
);

  wire not_1_out, not_2_out;

  not not_1 (not_1_out, Input_1);
  not not_2 (not_2_out, Input_0);
  and and_1 (out_6, not_2_out, not_1_out);
  and and_2 (out_5, Input_0, not_1_out);
  and and_3 (out_4, not_2_out, Input_1);
  and and_4 (out_3, Input_0, Input_1);
endmodule
