// Logisim project ALU.circ as structural Verilog: 8 circuits, main circuit ALU
module ALU (
  input  [2:0] ALU_OP,
  input  [3:0] Input_A,
  input  [3:0] Input_B,
  output [3:0] Output,
  output [3:0] Status_register
);

  wire and_1_out, and_2_out, not_1_out, not_2_out, not_3_out;
  wire [3:0] add_1_s, bit_extender_1_out, divider_1_out, multiplier_1_out, negator_1_out, sh_l_1_output,
       sh_r_1_p3, sub_1_s;

  ADD add_1 (.in_2(Input_A), .in_3(Input_B), .S(add_1_s), .Cin(1'b0));  // open: Overflow, Cout
  SUB sub_1 (.in_2(Input_A), .in_3(Input_B), .S(sub_1_s), .Cin(1'b0));  // open: Overflow, Cout
  Multiplier #(.width(4)) multiplier_1 (.a(Input_A), .b(Input_B), .out(multiplier_1_out));  // open: cin, cout
  Divider #(.width(4)) divider_1 (.a(Input_A), .b(Input_B), .out(divider_1_out));  // open: upper, rem
  CMP_4bit cmp_4bit_1 (.A(Input_A), .B(Input_B), .S(Status_register[1]));
  // SH_R sh_r_1: pin names not known; wires that end beside it: Input_A, Input_B[1:0], sh_r_1_p3
  SH_L sh_l_1 (.Input(Input_A), .Output(sh_l_1_output), .Sel(Input_B[1:0]));
  Negator #(.width(4)) negator_1 (.in(Input_A), .out(negator_1_out));
  assign bit_extender_1_out = {{3{1'b0}}, 1'b0};  // Bit_Extender bit_extender_1
  not not_1 (not_1_out, Input_A[3]);
  not not_2 (not_2_out, Input_B[3]);
  Multiplexer #(.select(3), .width(4), .enable("false")) multiplexer_1 (
    .in0(bit_extender_1_out), .in1(add_1_s), .in2(sub_1_s), .in3(multiplier_1_out), .in4(divider_1_out),
    .in5(sh_r_1_p3), .in6(sh_l_1_output), .in7(negator_1_out), .out(Output), .sel(ALU_OP));
  not not_3 (not_3_out, Output[3]);
  and and_1 (and_1_out, Output[3], not_1_out, not_2_out);
  and and_2 (and_2_out, not_3_out, Input_A[3], Input_B[3]);
  nor nor_1 (Status_register[0], Output[0], Output[1], Output[2], Output[3]);
  or or_1 (Status_register[3], and_1_out, and_2_out);
  LED Z (.in(Status_register[0]));
  LED Equality (.in(Status_register[1]));
  LED Negative (.in(Output[3]));
  LED Overflow (.in(Status_register[3]));

  assign Status_register[2] = Output[3];
endmodule

module CMP_4bit (
  input  [3:0] A,
  input  [3:0] B,
  output S
);

  wire xnor_1_out, xnor_2_out, xnor_3_out, xnor_4_out;

  xnor xnor_1 (xnor_1_out, A[0], B[0]);
  xnor xnor_2 (xnor_2_out, A[1], B[1]);
  xnor xnor_3 (xnor_3_out, A[2], B[2]);
  xnor xnor_4 (xnor_4_out, A[3], B[3]);
  and and_1 (S, xnor_1_out, xnor_2_out, xnor_3_out, xnor_4_out);
endmodule

module SH_R (
  input  [1:0] Sel,
  input  [3:0] Input,
  output [3:0] Output
);

  Multiplexer #(.select(2), .enable("false")) multiplexer_1 (
    .in0(Input[0]), .in1(Input[1]), .in2(Input[2]), .in3(Input[3]), .out(Output[0]), .sel(Sel));
  Multiplexer #(.select(2), .enable("false")) multiplexer_2 (
    .in0(Input[1]), .in1(Input[2]), .in2(Input[3]), .in3(1'b0), .out(Output[1]), .sel(Sel));
  Multiplexer #(.select(2), .enable("false")) multiplexer_3 (
    .in0(Input[2]), .in1(Input[3]), .in2(1'b0), .in3(1'b0), .out(Output[2]), .sel(Sel));
  Multiplexer #(.select(2), .enable("false")) multiplexer_4 (
    .in0(Input[3]), .in1(1'b0), .in2(1'b0), .in3(1'b0), .out(Output[3]), .sel(Sel));
endmodule

module SH_L (
  input  [1:0] Sel,
  input  [3:0] Input,
  output [3:0] Output
);

  Multiplexer #(.select(2), .enable("false")) multiplexer_1 (
    .in0(Input[0]), .in1(1'b0), .in2(1'b0), .in3(1'b0), .out(Output[0]), .sel(Sel));
  Multiplexer #(.select(2), .enable("false")) multiplexer_2 (
    .in0(Input[1]), .in1(Input[0]), .in2(1'b0), .in3(1'b0), .out(Output[1]), .sel(Sel));
  Multiplexer #(.select(2), .enable("false")) multiplexer_3 (
    .in0(Input[2]), .in1(Input[1]), .in2(Input[0]), .in3(1'b0), .out(Output[2]), .sel(Sel));
  Multiplexer #(.select(2), .enable("false")) multiplexer_4 (
    .in0(Input[3]), .in1(Input[2]), .in2(Input[1]), .in3(Input[0]), .out(Output[3]), .sel(Sel));
endmodule

module FS (
  input  Cin,
  input  A,
  input  B,
  output S,
  output Cout
);

  wire and_1_out, and_2_out, and_3_out, not_1_out;

  not not_1 (not_1_out, A);
  ExactlyOne xor_1 (.out(S), .in0(Cin), .in1(A), .in2(B));
  and and_1 (and_1_out, B, not_1_out);
  and and_2 (and_2_out, B, Cin);
  and and_3 (and_3_out, not_1_out, Cin);
  or or_1 (Cout, and_1_out, and_2_out, and_3_out);
endmodule

module FA (
  input  Cin,
  input  A,
  input  B,
  output S,
  output Cout
);

  wire and_1_out, and_2_out, and_3_out;

  ExactlyOne xor_1 (.out(S), .in0(Cin), .in1(A), .in2(B));
  and and_1 (and_1_out, B, A);
  and and_2 (and_2_out, B, Cin);
  and and_3 (and_3_out, A, Cin);
  or or_1 (Cout, and_1_out, and_2_out, and_3_out);
endmodule

module SUB (
  input  Cin,
  input  [3:0] in_2,
  input  [3:0] in_3,
  output [3:0] S,
  output Overflow,
  output Cout
);

  wire fs_1_cout, fs_2_cout, fs_3_cout;

  FS fs_1 (.A(in_2[0]), .B(in_3[0]), .S(S[0]), .Cin(Cin), .Cout(fs_1_cout));
  FS fs_2 (.A(in_2[1]), .B(in_3[1]), .S(S[1]), .Cin(fs_1_cout), .Cout(fs_2_cout));
  FS fs_3 (.A(in_2[2]), .B(in_3[2]), .S(S[2]), .Cin(fs_2_cout), .Cout(fs_3_cout));
  FS fs_4 (.A(in_2[3]), .B(in_3[3]), .S(S[3]), .Cin(fs_3_cout), .Cout(Cout));
  xor xor_1 (Overflow, fs_3_cout, Cout);
endmodule

module ADD (
  input  Cin,
  input  [3:0] in_2,
  input  [3:0] in_3,
  output [3:0] S,
  output Overflow,
  output Cout
);

  wire fa_1_cout, fa_2_cout, fa_3_cout;

  FA fa_1 (.A(in_2[0]), .B(in_3[0]), .S(S[0]), .Cin(Cin), .Cout(fa_1_cout));
  FA fa_2 (.A(in_2[1]), .B(in_3[1]), .S(S[1]), .Cin(fa_1_cout), .Cout(fa_2_cout));
  FA fa_3 (.A(in_2[2]), .B(in_3[2]), .S(S[2]), .Cin(fa_2_cout), .Cout(fa_3_cout));
  FA fa_4 (.A(in_2[3]), .B(in_3[3]), .S(S[3]), .Cin(fa_3_cout), .Cout(Cout));
  xor xor_1 (Overflow, fa_3_cout, Cout);
endmodule
