// Logisim project CMP-4bit.circ as structural Verilog: 1 circuit, main circuit CMP-4bit
module CMP_4bit (
  input  [3:0] A,
  input  [3:0] B,
  output S
);

  wire xnor_1_out, xnor_2_out, xnor_3_out, xnor_4_out;

  xnor xnor_1 (xnor_1_out, A[0], B[0]);
  xnor xnor_2 (xnor_2_out, A[1], B[1]);
  xnor xnor_3 (xnor_3_out, A[2], B[2]);
  xnor xnor_4 (xnor_4_out, A[3], B[3]);
  and and_1 (S, xnor_1_out, xnor_2_out, xnor_3_out, xnor_4_out);
endmodule
