// Logisim project CSR.circ as structural Verilog: 1 circuit, main circuit CSR
module CSR (
  input  clk,
  input  Write,
  input  [16:0] \input ,
  output RFxy,
  output RFsrc,
  output PC_plus_plus,
  output ARw,
  output SRw,
  output CD,
  output BR,
  output AD4,
  output AD3,
  output AD2,
  output AD1,
  output AD0,
  output RFw,
  output DRsrc,
  output IRw,
  output DRw,
  output MEMw
);

  D_Flip_Flop d_ff_1 (.clk(clk), .D(\input [0]), .Q(AD0), .en(Write));  // open: Qn, preset, reset
  D_Flip_Flop d_ff_2 (.clk(clk), .D(\input [1]), .Q(AD1), .en(Write));  // open: Qn, preset, reset
  D_Flip_Flop d_ff_3 (.clk(clk), .D(\input [2]), .Q(AD2), .en(Write));  // open: Qn, preset, reset
  D_Flip_Flop d_ff_4 (.clk(clk), .D(\input [3]), .Q(AD3), .en(Write));  // open: Qn, preset, reset
  D_Flip_Flop d_ff_5 (.clk(clk), .D(\input [4]), .Q(AD4), .en(Write));  // open: Qn, preset, reset
  D_Flip_Flop d_ff_6 (.clk(clk), .D(\input [5]), .Q(BR), .en(Write));  // open: Qn, preset, reset
  D_Flip_Flop d_ff_7 (.clk(clk), .D(\input [6]), .Q(CD), .en(Write));  // open: Qn, preset, reset
  D_Flip_Flop d_ff_8 (.clk(clk), .D(\input [7]), .Q(MEMw), .en(Write));  // open: Qn, preset, reset
  D_Flip_Flop d_ff_9 (.clk(clk), .D(\input [8]), .Q(SRw), .en(Write));  // open: Qn, preset, reset
  D_Flip_Flop d_ff_10 (.clk(clk), .D(\input [9]), .Q(DRw), .en(Write));  // open: Qn, preset, reset
  D_Flip_Flop d_ff_11 (.clk(clk), .D(\input [10]), .Q(ARw), .en(Write));  // open: Qn, preset, reset
  D_Flip_Flop d_ff_12 (.clk(clk), .D(\input [11]), .Q(IRw), .en(Write));  // open: Qn, preset, reset
  D_Flip_Flop d_ff_13 (.clk(clk), .D(\input [12]), .Q(PC_plus_plus), .en(Write));  // open: Qn, preset, reset
  D_Flip_Flop d_ff_14 (.clk(clk), .D(\input [13]), .Q(DRsrc), .en(Write));  // open: Qn, preset, reset
  D_Flip_Flop d_ff_15 (.clk(clk), .D(\input [14]), .Q(RFsrc), .en(Write));  // open: Qn, preset, reset
  D_Flip_Flop d_ff_16 (.clk(clk), .D(\input [15]), .Q(RFw), .en(Write));  // open: Qn, preset, reset
  D_Flip_Flop d_ff_17 (.clk(clk), .D(\input [16]), .Q(RFxy), .en(Write));  // open: Qn, preset, reset
endmodule
