// Logisim project Counter.circ as structural Verilog: 1 circuit, main circuit PC (counter)
module PC__counter (
  input  clk,
  input  enable,
  output [3:0] \output 
);

  Counter #(.width(4), .max('hf)) counter_1 (.count(enable), .Q(\output ), .clk(clk));  // open: load, D, carry, clr
endmodule
