// Logisim project Full-Adder.circ as structural Verilog: 1 circuit, main circuit Full-Adder
module Full_Adder (
  input  Cin,
  input  A,
  input  B,
  output S,
  output Cout
);

  wire and_1_out, and_2_out, and_3_out;

  ExactlyOne xor_1 (.out(S), .in0(Cin), .in1(A), .in2(B));
  and and_1 (and_1_out, B, A);
  and and_2 (and_2_out, B, Cin);
  and and_3 (and_3_out, A, Cin);
  or or_1 (Cout, and_1_out, and_2_out, and_3_out);
endmodule
