// Logisim project Mapper.circ as structural Verilog: 1 circuit, main circuit Mapeer
module Mapeer (
  input  [3:0] OPcode,
  output [4:0] control
);

  wire not_1_out, not_2_out, or_1_out, or_2_out;

  not not_1 (not_1_out, OPcode[0]);
  not not_2 (not_2_out, OPcode[1]);
  or or_1 (or_1_out, OPcode[0], OPcode[1]);
  or or_2 (or_2_out, OPcode[2], OPcode[3]);
  and and_1 (control[2], or_1_out, or_2_out);
  and and_2 (control[3], not_1_out, not_2_out, OPcode[2]);

  assign {control[4], control[1:0]} = {OPcode[3], 2'b00};
endmodule
