// Logisim project Mux 2-1 (2 bits).circ as structural Verilog: 1 circuit, main circuit Mux 2-1 (2 bits)
module Mux_2_1__2_bits (
  input  S,
  input  [1:0] Input_0,
  input  [1:0] Input_1,
  output [1:0] Output
);

  Mux_2_1 mux_2_1_1 (.A(Input_0[0]), .B(Input_1[0]), .Output(Output[0]), .S(S));
  Mux_2_1 mux_2_1_2 (.A(Input_0[1]), .B(Input_1[1]), .Output(Output[1]), .S(S));
endmodule
