// Logisim project Mux 2-1 (4 bits).circ as structural Verilog: 1 circuit, main circuit Mux 2-1 (4 bits)
module Mux_2_1__4_bits (
  input  in_1,
  input  [3:0] in_2,
  input  [3:0] in_3,
  output [3:0] out_4
);

  Mux_2_1 mux_2_1_1 (.A(in_2[0]), .B(in_3[0]), .Output(out_4[0]), .S(in_1));
  Mux_2_1 mux_2_1_2 (.A(in_2[1]), .B(in_3[1]), .Output(out_4[1]), .S(in_1));
  Mux_2_1 mux_2_1_3 (.A(in_2[2]), .B(in_3[2]), .Output(out_4[2]), .S(in_1));
  Mux_2_1 mux_2_1_4 (.A(in_2[3]), .B(in_3[3]), .Output(out_4[3]), .S(in_1));
endmodule
