// Logisim project Mux 2-1.circ as structural Verilog: 1 circuit, main circuit Mux 2-1
module Mux_2_1 (
  input  S,
  input  A,
  input  B,
  output Output
);

  wire and_1_out, and_2_out, not_1_out;

  not not_1 (not_1_out, S);
  and and_1 (and_1_out, not_1_out, A);
  and and_2 (and_2_out, S, B);
  or or_1 (Output, and_1_out, and_2_out);
endmodule
