// Logisim project Mux 4-1 (4 bits).circ as structural Verilog: 1 circuit, main circuit Mux 4-1 (4 bits)
module Mux_4_1__4_bits (
  input  Sel_0,
  input  Sel_1,
  input  [3:0] In_0,
  input  [3:0] In_1,
  input  [3:0] In_2,
  input  [3:0] In_3,
  output [3:0] out_7
);

  wire [3:0] mux_2_1_4_bits_1_out_4, mux_2_1_4_bits_2_out_4;

  Mux_2_1__4_bits mux_2_1_4_bits_1 (.in_2(In_0), .in_3(In_1), .out_4(mux_2_1_4_bits_1_out_4), .in_1(Sel_0));
  Mux_2_1__4_bits mux_2_1_4_bits_2 (.in_2(In_2), .in_3(In_3), .out_4(mux_2_1_4_bits_2_out_4), .in_1(Sel_0));
  Mux_2_1__4_bits mux_2_1_4_bits_3 (
    .in_2(mux_2_1_4_bits_1_out_4), .in_3(mux_2_1_4_bits_2_out_4), .out_4(out_7), .in_1(Sel_1));
endmodule
