// Logisim project Mux 4-1.circ as structural Verilog: 1 circuit, main circuit Mux 4-1
module Mux_4_1 (
  input  Sel_0,
  input  Sel_1,
  input  in_3,
  input  in_4,
  input  in_5,
  input  in_6,
  output out_7
);

  wire mux_2_1_1_output, mux_2_1_2_output;

  Mux_2_1 mux_2_1_1 (.A(in_3), .B(in_4), .Output(mux_2_1_1_output), .S(Sel_0));
  Mux_2_1 mux_2_1_2 (.A(in_5), .B(in_6), .Output(mux_2_1_2_output), .S(Sel_0));
  Mux_2_1 mux_2_1_3 (.A(mux_2_1_1_output), .B(mux_2_1_2_output), .Output(out_7), .S(Sel_1));
endmodule
