// Logisim project Mux 8-1 (4 bits).circ as structural Verilog: 1 circuit, main circuit Mux 8-1 (4 bits)
module Mux_8_1__4_bits (
  input  [2:0] Select,
  input  [3:0] Input_0,
  input  [3:0] Input_1,
  input  [3:0] Input_2,
  input  [3:0] Input_3,
  input  [3:0] Input_4,
  input  [3:0] Input_5,
  input  [3:0] Input_6,
  input  [3:0] Input_7,
  output [3:0] Output
);

  wire [3:0] mux_4_1_4_bits_1_out_7, mux_4_1_4_bits_2_out_7;

  Mux_4_1__4_bits mux_4_1_4_bits_1 (
    .In_0(Input_0), .In_1(Input_1), .In_2(Input_2), .In_3(Input_3), .out_7(mux_4_1_4_bits_1_out_7),
    .Sel_0(Select[0]), .Sel_1(Select[1]));
  Mux_4_1__4_bits mux_4_1_4_bits_2 (
    .In_0(Input_4), .In_1(Input_5), .In_2(Input_6), .In_3(Input_7), .out_7(mux_4_1_4_bits_2_out_7),
    .Sel_0(Select[0]), .Sel_1(Select[1]));
  Mux_2_1__4_bits mux_2_1_4_bits_1 (
    .in_2(mux_4_1_4_bits_1_out_7), .in_3(mux_4_1_4_bits_2_out_7), .out_4(Output), .in_1(Select[2]));
endmodule
