// Logisim project PC.circ as structural Verilog: 1 circuit, main circuit PC
module PC (
  input  clk,
  input  write,
  input  [4:0] Input,
  output [4:0] Output
);

  Counter #(.width(5), .max('h1f)) counter_1 (
    .load(write), .D(Input), .count(write), .Q(Output), .clk(clk));  // open: carry, clr
endmodule
