// Logisim project RF.circ as structural Verilog: 1 circuit, main circuit RF
module RF (
  input  [1:0] Select,
  input  [1:0] X,
  input  [1:0] Y,
  input  clk,
  input  Write,
  input  [3:0] Input,
  output [3:0] Output_X,
  output [3:0] Output_Y
);

  wire and_1_out, and_2_out, and_3_out, and_4_out, decoder_1_out0, decoder_1_out1, decoder_1_out2,
       decoder_1_out3;
  wire [3:0] register_4_bits_1_output, register_4_bits_2_output, register_4_bits_3_output,
       register_4_bits_4_output;

  Decoder #(.select(2), .enable("false")) decoder_1 (
    .out0(decoder_1_out0), .out1(decoder_1_out1), .out2(decoder_1_out2), .out3(decoder_1_out3), .sel(Select));
  and and_1 (and_1_out, Write, decoder_1_out0);
  and and_2 (and_2_out, Write, decoder_1_out1);
  and and_3 (and_3_out, Write, decoder_1_out2);
  and and_4 (and_4_out, Write, decoder_1_out3);
  Register__4_bits register_4_bits_1 (.in_3(Input), .Output(register_4_bits_1_output), .Write(and_1_out), .clk(clk));
  Register__4_bits register_4_bits_2 (.in_3(Input), .Output(register_4_bits_2_output), .Write(and_2_out), .clk(clk));
  Register__4_bits register_4_bits_3 (.in_3(Input), .Output(register_4_bits_3_output), .Write(and_3_out), .clk(clk));
  Register__4_bits register_4_bits_4 (.in_3(Input), .Output(register_4_bits_4_output), .Write(and_4_out), .clk(clk));
  Mux_4_1__4_bits mux_4_1_4_bits_1 (
    .In_0(register_4_bits_1_output), .In_1(register_4_bits_2_output), .In_2(register_4_bits_3_output),
    .In_3(register_4_bits_4_output), .out_7(Output_X), .Sel_0(X[0]), .Sel_1(X[1]));
  Mux_4_1__4_bits mux_4_1_4_bits_2 (
    .In_0(register_4_bits_1_output), .In_1(register_4_bits_2_output), .In_2(register_4_bits_3_output),
    .In_3(register_4_bits_4_output), .out_7(Output_Y), .Sel_0(Y[0]), .Sel_1(Y[1]));
endmodule
