// Logisim project RI.circ as structural Verilog: 1 circuit, main circuit RI
module RI (
  input  clk,
  input  Write,
  input  [11:0] \input ,
  output _11,
  output _10,
  output _9,
  output _8,
  output _7,
  output _6,
  output _5,
  output _4,
  output _3,
  output _2,
  output _1,
  output _0
);

  D_Flip_Flop d_ff_1 (.clk(clk), .D(\input [0]), .Q(_0), .en(Write));  // open: Qn, preset, reset
  D_Flip_Flop d_ff_2 (.clk(clk), .D(\input [1]), .Q(_1), .en(Write));  // open: Qn, preset, reset
  D_Flip_Flop d_ff_3 (.clk(clk), .D(\input [2]), .Q(_2), .en(Write));  // open: Qn, preset, reset
  D_Flip_Flop d_ff_4 (.clk(clk), .D(\input [3]), .Q(_3), .en(Write));  // open: Qn, preset, reset
  D_Flip_Flop d_ff_5 (.clk(clk), .D(\input [4]), .Q(_4), .en(Write));  // open: Qn, preset, reset
  D_Flip_Flop d_ff_6 (.clk(clk), .D(\input [5]), .Q(_5), .en(Write));  // open: Qn, preset, reset
  D_Flip_Flop d_ff_7 (.clk(clk), .D(\input [6]), .Q(_6), .en(Write));  // open: Qn, preset, reset
  D_Flip_Flop d_ff_8 (.clk(clk), .D(\input [7]), .Q(_7), .en(Write));  // open: Qn, preset, reset
  D_Flip_Flop d_ff_9 (.clk(clk), .D(\input [8]), .Q(_8), .en(Write));  // open: Qn, preset, reset
  D_Flip_Flop d_ff_10 (.clk(clk), .D(\input [9]), .Q(_9), .en(Write));  // open: Qn, preset, reset
  D_Flip_Flop d_ff_11 (.clk(clk), .D(\input [10]), .Q(_10), .en(Write));  // open: Qn, preset, reset
  D_Flip_Flop d_ff_12 (.clk(clk), .D(\input [11]), .Q(_11), .en(Write));  // open: Qn, preset, reset
endmodule
