// Logisim project Register (4 bits).circ as structural Verilog: 1 circuit, main circuit Register (4 bits)
module Register__4_bits (
  input  clk,
  input  Write,
  input  [3:0] in_3,
  output [3:0] Output
);

  D_Flip_Flop d_ff_1 (.clk(clk), .D(in_3[0]), .Q(Output[0]), .en(Write));  // open: Qn, preset, reset
  D_Flip_Flop d_ff_2 (.clk(clk), .D(in_3[1]), .Q(Output[1]), .en(Write));  // open: Qn, preset, reset
  D_Flip_Flop d_ff_3 (.clk(clk), .D(in_3[2]), .Q(Output[2]), .en(Write));  // open: Qn, preset, reset
  D_Flip_Flop d_ff_4 (.clk(clk), .D(in_3[3]), .Q(Output[3]), .en(Write));  // open: Qn, preset, reset
endmodule
