// Logisim project Shifter-R (4bit).circ as structural Verilog: 1 circuit, main circuit Shifter-R (4bit)
module Shifter_R__4bit (
  input  [1:0] Sel,
  input  [3:0] Input,
  output [3:0] Output
);

  Mux_4_1 mux_4_1_1 (
    .in_3(Input[0]), .in_4(Input[1]), .in_5(Input[2]), .in_6(Input[3]), .out_7(Output[0]), .Sel_0(Sel[0]),
    .Sel_1(Sel[1]));
  Mux_4_1 mux_4_1_2 (
    .in_3(Input[1]), .in_4(Input[2]), .in_5(Input[3]), .in_6(1'b0), .out_7(Output[1]), .Sel_0(Sel[0]),
    .Sel_1(Sel[1]));
  Mux_4_1 mux_4_1_3 (
    .in_3(Input[2]), .in_4(Input[3]), .in_5(1'b0), .in_6(1'b0), .out_7(Output[2]), .Sel_0(Sel[0]),
    .Sel_1(Sel[1]));
  Mux_4_1 mux_4_1_4 (
    .in_3(Input[3]), .in_4(1'b0), .in_5(1'b0), .in_6(1'b0), .out_7(Output[3]), .Sel_0(Sel[0]), .Sel_1(Sel[1]));
endmodule
