// Logisim project Sub 4 bits.circ as structural Verilog: 1 circuit, main circuit Sub 4 bits
module Sub_4_bits (
  input  Cin,
  input  [3:0] in_2,
  input  [3:0] in_3,
  output [3:0] S,
  output Overflow,
  output Cout
);

  wire full_sub_1_cout, full_sub_2_cout, full_sub_3_cout;

  Full_Sub full_sub_1 (.A(in_2[0]), .B(in_3[0]), .S(S[0]), .Cin(Cin), .Cout(full_sub_1_cout));
  Full_Sub full_sub_2 (.A(in_2[1]), .B(in_3[1]), .S(S[1]), .Cin(full_sub_1_cout), .Cout(full_sub_2_cout));
  Full_Sub full_sub_3 (.A(in_2[2]), .B(in_3[2]), .S(S[2]), .Cin(full_sub_2_cout), .Cout(full_sub_3_cout));
  Full_Sub full_sub_4 (.A(in_2[3]), .B(in_3[3]), .S(S[3]), .Cin(full_sub_3_cout), .Cout(Cout));
  xor xor_1 (Overflow, full_sub_3_cout, Cout);
endmodule
