// Logisim project UAL.circ as structural Verilog: 1 circuit, main circuit UAL
module UAL (
  input  ALU_OP__2_minus,
  input  ALU_OP__0_minus,
  input  ALU_OP__1_minus,
  input  [3:0] Input_A,
  input  [3:0] Input_B,
  output [3:0] Output,
  output Equality,
  output Negative_Output,
  output Overflow
);

  wire and_1_out, and_2_out, not_1_out, not_2_out;
  wire [3:0] adder_4_bits_1_s, bit_extender_1_out, divider_1_out, multiplier_1_out, negator_1_out,
       shifter_l_4bit_1_output, shifter_r_4bit_1_output, sub_4_bits_1_s;

  Adder_4_bits adder_4_bits_1 (
    .in_2(Input_A), .in_3(Input_B), .S(adder_4_bits_1_s), .Cin(1'b0));  // open: Overflow, Cout
  Sub_4_bits sub_4_bits_1 (.in_2(Input_A), .in_3(Input_B), .S(sub_4_bits_1_s), .Cin(1'b0));  // open: Overflow, Cout
  Multiplier #(.width(4)) multiplier_1 (.a(Input_A), .b(Input_B), .out(multiplier_1_out));  // open: cin, cout
  Divider #(.width(4)) divider_1 (.a(Input_A), .b(Input_B), .out(divider_1_out));  // open: upper, rem
  Comparator #(.width(4)) comparator_1 (.a(Input_A), .b(Input_B), .eq(Equality));  // open: gt, lt
  Shifter_R__4bit shifter_r_4bit_1 (.Input(Input_A), .Output(shifter_r_4bit_1_output), .Sel(Input_B[1:0]));
  Shifter_L_4bit shifter_l_4bit_1 (.Input(Input_A), .Output(shifter_l_4bit_1_output), .Sel(Input_B[1:0]));
  Negator #(.width(4)) negator_1 (.in(Input_A), .out(negator_1_out));
  assign bit_extender_1_out = {{3{1'b0}}, 1'b0};  // Bit_Extender bit_extender_1
  not not_1 (not_1_out, Input_A[3]);
  not not_2 (not_2_out, Input_B[3]);
  Mux_8_1__4_bits mux_8_1_4_bits_1 (
    .Input_0(bit_extender_1_out), .Input_1(adder_4_bits_1_s), .Input_2(sub_4_bits_1_s),
    .Input_3(multiplier_1_out), .Input_4(divider_1_out), .Input_5(shifter_r_4bit_1_output),
    .Input_6(shifter_l_4bit_1_output), .Input_7(negator_1_out), .Output(Output),
    .Select({ALU_OP__2_minus, ALU_OP__1_minus, ALU_OP__0_minus}));
  and and_1 (and_1_out, Output[3], not_1_out, not_2_out);
  and and_2 (and_2_out, Output[3], Input_A[3], Input_B[3]);
  or or_1 (Negative_Output, and_1_out, and_2_out);
  LED u_Equality (.in(Equality));
  LED Negative (.in(Output[3]));
  LED u_Overflow (.in(Negative_Output));

  assign Overflow = Output[3];
endmodule
