// Logisim project UCC.circ as structural Verilog: 1 circuit, main circuit UCC
module UCC (
  input  clk,
  input  Input,
  input  [3:0] OPcode,
  output out_4,
  output out_5,
  output out_6,
  output out_7,
  output out_8,
  output out_9,
  output out_10,
  output out_11,
  output out_12,
  output out_13
);

  wire csr_1_br, csr_1_cd, not_1_out, or_1_out;
  wire [4:0] csr_1_ad0, mapeer_1_control, mux_2_1_5_bits_1_out_4, pc_1_output;
  wire [16:0] rom_1_data;

  Mapeer mapeer_1 (.OPcode(OPcode), .control(mapeer_1_control));
  or or_1 (or_1_out, not_1_out, Input);
  PC pc_1 (.Input(mux_2_1_5_bits_1_out_4), .Output(pc_1_output), .clk(clk), .write(or_1_out));
  Mux_2_1__5_bits mux_2_1_5_bits_1 (
    .in_2(mapeer_1_control), .in_3(csr_1_ad0), .out_4(mux_2_1_5_bits_1_out_4), .in_1(csr_1_br));
  not not_1 (not_1_out, csr_1_cd);
  ROM #(.addrWidth(5), .dataWidth(17)) rom_1 (.addr(pc_1_output), .data(rom_1_data));  // open: sel
  CSR csr_1 (
    .\input (rom_1_data), .clk(clk), .Write(1'b1), .RFxy(out_4), .RFw(out_5), .RFsrc(out_6), .DRsrc(out_7),
    .PC_plus_plus(out_8), .IRw(out_9), .ARw(out_10), .DRw(out_11), .SRw(out_12), .MEMw(out_13),
    .CD(csr_1_cd), .BR(csr_1_br), .AD4(csr_1_ad0[4]), .AD3(csr_1_ad0[3]), .AD2(csr_1_ad0[2]),
    .AD1(csr_1_ad0[1]), .AD0(csr_1_ad0[0]));

  // Notes on the sheet:
  //   contents of rom_1 (hex, n*v repeats v):
  //   c018 0 0 0 c018 0 0 0 10118
endmodule
